// Logisim project BranchingModule.circ as structural Verilog: 1 circuit, main circuit branchDetector
module branchDetector (
  input  [31:0] dataA,
  input  [31:0] dataB,
  input  branchUnsigned,
  output branchEquals,
  output branchLessThan
);

  wire comparator_1_lt, comparator_2_lt;

  Comparator #(.width(32)) comparator_1 (.a(dataA), .b(dataB), .eq(branchEquals), .lt(comparator_1_lt));  // open: gt
  Multiplexer multiplexer_1 (.in0(comparator_1_lt), .in1(comparator_2_lt), .out(branchLessThan), .sel(branchUnsigned));
  Comparator #(.mode("unsigned"), .width(32)) comparator_2 (
    .a(dataA), .b(dataB), .lt(comparator_2_lt));  // open: gt, eq
endmodule
