// Logisim project Computor.circ as structural Verilog: 1 circuit, main circuit main
module main (
  input  [31:0] instruction,
  output [31:0] result
);

  wire alu_1_p4, alu_1_p6, alu_1_p8, clock_1_out, decodemodule_1_regload;
  wire [3:0] decodemodule_1_alu_select;
  wire [4:0] decodemodule_1_rd_i, decodemodule_1_rs1_i, decodemodule_1_rs2_i;
  wire [31:0] decodemodule_1_datab, registerfile32_1_rs1, registerfile32_1_rs2;

  Clock clock_1 (.out(clock_1_out));
  DecodeModule decodemodule_1 (
    .RegFile_rs2(registerfile32_1_rs2), .instruction(instruction), .dataB(decodemodule_1_datab),
    .rd_i(decodemodule_1_rd_i), .RegLoad(decodemodule_1_regload), .rs1_i(decodemodule_1_rs1_i),
    .ALU_select(decodemodule_1_alu_select), .rs2_i(decodemodule_1_rs2_i));
  RegisterFile32 registerfile32_1 (
    .load(decodemodule_1_regload), .rsi1(decodemodule_1_rs1_i), .rsi2(decodemodule_1_rs2_i),
    .rdi(decodemodule_1_rd_i), .rd(result), .clock(clock_1_out), .rs1(registerfile32_1_rs1),
    .rs2(registerfile32_1_rs2));
  // ALU alu_1: pin names not known; wires that end beside it: decodemodule_1_alu_select, registerfile32_1_rs1, decodemodule_1_datab, alu_1_p4, alu_1_p4, alu_1_p6, alu_1_p6, alu_1_p8, alu_1_p8, result
endmodule
