// Logisim project DecodeModule.circ as structural Verilog: 6 circuits, main circuit R_controller
module R_controller (
  input  Opcode_b2,
  input  Opcode_b3,
  input  Opcode_b4,
  input  Opcode_b5,
  input  Opcode_b6,
  input  Funct_3_b12,
  input  Funct_3_b13,
  input  Funct_3_b14,
  input  Funct_7_b30,
  output add,
  output sub,
  output s_ll,
  output s_lt,
  output s_ltu,
  output x_or,
  output s_rl,
  output s_ra,
  output o_r,
  output a_nd
);

  and and_1 (add, ~Opcode_b2, ~Opcode_b3, Opcode_b4, Opcode_b5, ~Opcode_b6, ~Funct_3_b12, ~Funct_3_b13, ~Funct_3_b14, ~Funct_7_b30);  // AND_Gate
  and and_2 (sub, ~Opcode_b2, ~Opcode_b3, Opcode_b4, Opcode_b5, ~Opcode_b6, ~Funct_3_b12, ~Funct_3_b13, ~Funct_3_b14, Funct_7_b30);  // AND_Gate
  and and_3 (s_ll, ~Opcode_b2, ~Opcode_b3, Opcode_b4, Opcode_b5, ~Opcode_b6, Funct_3_b12, ~Funct_3_b13, ~Funct_3_b14, ~Funct_7_b30);  // AND_Gate
  and and_4 (s_lt, ~Opcode_b2, ~Opcode_b3, Opcode_b4, Opcode_b5, ~Opcode_b6, ~Funct_3_b12, Funct_3_b13, ~Funct_3_b14, ~Funct_7_b30);  // AND_Gate
  and and_5 (s_ltu, ~Opcode_b2, ~Opcode_b3, Opcode_b4, Opcode_b5, ~Opcode_b6, Funct_3_b12, Funct_3_b13, ~Funct_3_b14, ~Funct_7_b30);  // AND_Gate
  and and_6 (x_or, ~Opcode_b2, ~Opcode_b3, Opcode_b4, Opcode_b5, ~Opcode_b6, ~Funct_3_b12, ~Funct_3_b13, Funct_3_b14, ~Funct_7_b30);  // AND_Gate
  and and_7 (s_rl, ~Opcode_b2, ~Opcode_b3, Opcode_b4, Opcode_b5, ~Opcode_b6, Funct_3_b12, ~Funct_3_b13, Funct_3_b14, ~Funct_7_b30);  // AND_Gate
  and and_8 (s_ra, ~Opcode_b2, ~Opcode_b3, Opcode_b4, Opcode_b5, ~Opcode_b6, Funct_3_b12, ~Funct_3_b13, Funct_3_b14, Funct_7_b30);  // AND_Gate
  and and_9 (o_r, ~Opcode_b2, ~Opcode_b3, Opcode_b4, Opcode_b5, ~Opcode_b6, ~Funct_3_b12, Funct_3_b13, Funct_3_b14, ~Funct_7_b30);  // AND_Gate
  and and_10 (a_nd, ~Opcode_b2, ~Opcode_b3, Opcode_b4, Opcode_b5, ~Opcode_b6, Funct_3_b12, Funct_3_b13, Funct_3_b14, ~Funct_7_b30);  // AND_Gate

  // Notes on the sheet:
  //   R_TYPE
  //   ADD
  //   SUB
  //   SLL
  //   SLT
  //   XOR
  //   SRL
  //   SRA
  //   OR
  //   AND
  //   SLTU
endmodule

module I_R_controller (
  input  Opcode_b2,
  input  Opcode_b3,
  input  Opcode_b4,
  input  Opcode_b5,
  input  Opcode_b6,
  input  Funct_3_b12,
  input  Funct_3_b13,
  input  Funct_3_b14,
  output addi,
  output slli,
  output slti,
  output sltiu,
  output xori,
  output srli,
  output srai,
  output ori,
  output andi
);

  and and_1 (addi, ~Opcode_b2, ~Opcode_b3, Opcode_b4, Opcode_b5, Funct_3_b12, ~Funct_3_b13, ~Funct_3_b14, ~1'b0);  // AND_Gate
  and and_2 (slli, ~Opcode_b2, ~Opcode_b3, Opcode_b4, Opcode_b5, Opcode_b6, Funct_3_b12, ~Funct_3_b13, ~Funct_3_b14, ~1'b0);  // AND_Gate
  and and_3 (slti, ~Opcode_b2, ~Opcode_b3, Opcode_b4, Opcode_b5, Opcode_b6, ~Funct_3_b12, Funct_3_b13, ~Funct_3_b14, ~1'b0);  // AND_Gate
  and and_4 (sltiu, ~Opcode_b2, ~Opcode_b3, Opcode_b4, Opcode_b5, Opcode_b6, Funct_3_b12, Funct_3_b13, ~Funct_3_b14, ~1'b0);  // AND_Gate
  and and_5 (xori, ~Opcode_b2, ~Opcode_b3, Opcode_b4, Opcode_b5, Opcode_b6, ~Funct_3_b12, ~Funct_3_b13, Funct_3_b14, ~1'b0);  // AND_Gate
  and and_6 (srli, ~Opcode_b2, ~Opcode_b3, Opcode_b4, Opcode_b5, Opcode_b6, Funct_3_b12, ~Funct_3_b13, Funct_3_b14, ~1'b0);  // AND_Gate
  and and_7 (srai, ~Opcode_b2, ~Opcode_b3, Opcode_b4, Opcode_b5, Opcode_b6, Funct_3_b12, ~Funct_3_b13, Funct_3_b14, ~1'b0);  // AND_Gate
  and and_8 (ori, ~Opcode_b2, ~Opcode_b3, Opcode_b4, Opcode_b5, Opcode_b6, ~Funct_3_b12, Funct_3_b13, Funct_3_b14, ~1'b0);  // AND_Gate
  and and_9 (andi, ~Opcode_b2, ~Opcode_b3, Opcode_b4, Opcode_b5, Opcode_b6, Funct_3_b12, Funct_3_b13, Funct_3_b14, ~1'b0);  // AND_Gate

  // Notes on the sheet:
  //   I_TYPE (but only R type equivalents)
  //   ADDI
  //   SLLI
  //   SLTI
  //   SRLI
  //   SRAI
  //   ORI
  //   ANDI
  //   SLTIU
  //   XORI
endmodule

module ControllSignalGenerator (
  input  [31:0] instruction,
  output RegWen,
  output RegRead,
  output [3:0] ALUselect,
  output [2:0] ImmGenSelect,
  output [2:0] MMU_sel
);

  wire i_l_controller_1_lb, i_l_controller_1_lbu, i_l_controller_1_lh, i_l_controller_1_lhu,
       i_r_controller_1_addi, i_r_controller_1_andi, i_r_controller_1_ori, i_r_controller_1_slli,
       i_r_controller_1_slti, i_r_controller_1_sltiu, i_r_controller_1_srai, i_r_controller_1_srli,
       i_r_controller_1_xori, r_controller_1_a_nd, r_controller_1_add, r_controller_1_o_r,
       r_controller_1_s_ll, r_controller_1_s_lt, r_controller_1_s_ltu, r_controller_1_s_ra,
       r_controller_1_s_rl, r_controller_1_sub, r_controller_1_x_or;

  I_L_controller i_l_controller_1 (
    .Opcode_b2(instruction[2]), .Opcode_b3(instruction[3]), .Opcode_b4(instruction[4]),
    .Opcode_b5(instruction[5]), .Opcode_b6(instruction[6]), .Funct_3_b12(instruction[12]),
    .Funct_3_b13(instruction[13]), .Funct_3_b14(instruction[14]), .lb(i_l_controller_1_lb),
    .lbu(i_l_controller_1_lbu), .lh(i_l_controller_1_lh), .lhu(i_l_controller_1_lhu), .lw(MMU_sel[2]));
  R_controller r_controller_1 (
    .Opcode_b2(instruction[2]), .Opcode_b3(instruction[3]), .Opcode_b4(instruction[4]),
    .Opcode_b5(instruction[5]), .Opcode_b6(instruction[6]), .Funct_3_b12(instruction[12]),
    .Funct_3_b13(instruction[13]), .Funct_3_b14(instruction[14]), .Funct_7_b30(instruction[30]),
    .add(r_controller_1_add), .sub(r_controller_1_sub), .s_ll(r_controller_1_s_ll),
    .s_lt(r_controller_1_s_lt), .s_ltu(r_controller_1_s_ltu), .x_or(r_controller_1_x_or),
    .s_rl(r_controller_1_s_rl), .s_ra(r_controller_1_s_ra), .o_r(r_controller_1_o_r),
    .a_nd(r_controller_1_a_nd));
  I_R_controller i_r_controller_1 (
    .Opcode_b2(instruction[2]), .Opcode_b3(instruction[3]), .Opcode_b4(instruction[4]),
    .Opcode_b5(instruction[5]), .Opcode_b6(instruction[6]), .Funct_3_b12(instruction[12]),
    .Funct_3_b13(instruction[13]), .Funct_3_b14(instruction[14]), .addi(i_r_controller_1_addi),
    .slli(i_r_controller_1_slli), .slti(i_r_controller_1_slti), .sltiu(i_r_controller_1_sltiu),
    .xori(i_r_controller_1_xori), .srli(i_r_controller_1_srli), .srai(i_r_controller_1_srai),
    .ori(i_r_controller_1_ori), .andi(i_r_controller_1_andi));
  or or_1 (RegRead, r_controller_1_add, r_controller_1_sub, r_controller_1_s_ll, r_controller_1_s_lt, r_controller_1_s_ltu, r_controller_1_x_or, r_controller_1_s_rl, r_controller_1_s_ra, r_controller_1_o_r, r_controller_1_a_nd);
  or or_2 (ALUselect[0], i_r_controller_1_andi, i_r_controller_1_srai, i_r_controller_1_srli, i_r_controller_1_sltiu, i_r_controller_1_slli, r_controller_1_a_nd, r_controller_1_s_ra, r_controller_1_s_rl, r_controller_1_s_ltu, r_controller_1_s_ll);
  or or_3 (ALUselect[1], r_controller_1_s_lt, r_controller_1_s_ltu, r_controller_1_o_r, r_controller_1_a_nd, i_r_controller_1_andi, i_r_controller_1_ori, i_r_controller_1_sltiu, i_r_controller_1_slti);
  or or_4 (ALUselect[2], i_r_controller_1_andi, i_r_controller_1_ori, i_r_controller_1_srai, i_r_controller_1_srli, i_r_controller_1_xori, r_controller_1_a_nd, r_controller_1_o_r, r_controller_1_s_ra, r_controller_1_s_rl, r_controller_1_x_or);
  or or_5 (ALUselect[3], r_controller_1_sub, r_controller_1_s_ra, i_r_controller_1_srai);
  or or_6 (MMU_sel[0], i_l_controller_1_lhu, i_l_controller_1_lbu);
  or or_7 (MMU_sel[1], i_l_controller_1_lhu, i_l_controller_1_lh);

  assign ImmGenSelect = 3'b000;
  assign RegWen = 1'b1;

  // Notes on the sheet:
  //   TRUTH TABLE : 
  //   https://docs.google.com/spreadsheets/d/1UNqJ4Yt46JSkYKQd5MZEKLEsWBbQFHRvYb_v7ItSYes/edit?usp=sharing
endmodule

module ImmediateSelector (
  input  [31:0] immediate_31_0,
  input  [31:0] rs2,
  input  readRegister,
  output [31:0] dataB
);

  Multiplexer #(.width(32)) multiplexer_1 (.in0(immediate_31_0), .in1(rs2), .out(dataB), .sel(readRegister));
endmodule

module DecodeModule (
  input  [31:0] instruction,
  output RegLoad,
  output RegRead,
  output [3:0] ALU_select,
  output [2:0] ImmediateGenSelect,
  output [2:0] MMU_sel,
  output [4:0] rd_i,
  output [4:0] rs1_i,
  output [4:0] rs2_i
);

  ControllSignalGenerator controllsignalgenerator_1 (
    .instruction(instruction), .RegWen(RegLoad), .RegRead(RegRead), .ALUselect(ALU_select),
    .ImmGenSelect(ImmediateGenSelect), .MMU_sel(MMU_sel));

  assign rd_i = instruction[11:7];
  assign rs1_i = instruction[19:15];
  assign rs2_i = instruction[24:20];
endmodule

module I_L_controller (
  input  Opcode_b2,
  input  Opcode_b3,
  input  Opcode_b4,
  input  Opcode_b5,
  input  Opcode_b6,
  input  Funct_3_b12,
  input  Funct_3_b13,
  input  Funct_3_b14,
  output lb,
  output lbu,
  output lh,
  output lhu,
  output lw
);

  and and_1 (lb, ~Opcode_b2, ~Opcode_b3, ~Opcode_b4, ~Opcode_b5, ~Opcode_b6, ~Funct_3_b12, ~Funct_3_b13, ~Funct_3_b14, ~1'b0);  // AND_Gate
  and and_2 (lbu, ~Opcode_b2, ~Opcode_b3, ~Opcode_b4, ~Opcode_b5, ~Opcode_b6, ~Funct_3_b12, ~Funct_3_b13, Funct_3_b14, ~1'b0);  // AND_Gate
  and and_3 (lh, ~Opcode_b2, ~Opcode_b3, ~Opcode_b4, ~Opcode_b5, ~Opcode_b6, Funct_3_b12, ~Funct_3_b13, ~Funct_3_b14, ~1'b0);  // AND_Gate
  and and_4 (lhu, ~Opcode_b2, ~Opcode_b3, ~Opcode_b4, ~Opcode_b5, ~Opcode_b6, Funct_3_b12, ~Funct_3_b13, Funct_3_b14, ~1'b0);  // AND_Gate
  and and_5 (lw, ~Opcode_b2, ~Opcode_b3, ~Opcode_b4, ~Opcode_b5, ~Opcode_b6, ~Funct_3_b12, Funct_3_b13, ~Funct_3_b14, ~1'b0);  // AND_Gate

  // Notes on the sheet:
  //   I_TYPE_(Load Instructions)
  //   LB
  //   LBU
  //   LH
  //   LHU
  //   LW
endmodule
