// Logisim project InstructionFetchModule.circ as structural Verilog: 1 circuit, main circuit ProgramCounter
module ProgramCounter (
  input  [31:0] Inp,
  input  isBranchTaken,
  input  clock,
  output [31:0] Outp
);

  wire adder_1_cout;
  wire [31:0] adder_1_out, multiplexer_1_out;

  Multiplexer #(.width(32)) multiplexer_1 (.in0(adder_1_out), .in1(Inp), .out(multiplexer_1_out), .sel(isBranchTaken));
  Register #(.width(32)) programCounter (.D(multiplexer_1_out), .en(1'b1), .clk(clock), .Q(Outp));  // open: clr
  Adder #(.width(32)) adder_1 (.a(32'h4), .b(Outp), .out(adder_1_out), .cin(1'b0), .cout(adder_1_cout));
  LED led_1 (.in(adder_1_cout));
endmodule
