// Logisim project MemoryModule.circ as structural Verilog: 1 circuit, main circuit memoryModule
module memoryModule (
  input  memLoad,
  input  clock,
  input  [31:0] data,
  input  [31:0] address,
  input  [2:0] funct_3,
  output [31:0] memOut
);

  wire [7:0] multiplexer_1_out;
  wire [15:0] multiplexer_2_out;
  wire [31:0] bit_extender_1_out, bit_extender_2_out, bit_extender_3_out, bit_extender_4_out, ram128kb_1_outp;

  Ram128KB ram128kb_1 (.load(memLoad), .clock(clock), .inp(data), .address(address), .outp(ram128kb_1_outp));
  Multiplexer #(.select(2), .width(8)) multiplexer_1 (
    .in0(ram128kb_1_outp[7:0]), .in1(ram128kb_1_outp[15:8]), .in2(ram128kb_1_outp[23:16]),
    .in3(ram128kb_1_outp[31:24]), .out(multiplexer_1_out), .sel(address[1:0]));
  Multiplexer #(.width(16)) multiplexer_2 (
    .in0(ram128kb_1_outp[15:0]), .in1(ram128kb_1_outp[31:16]), .out(multiplexer_2_out), .sel(address[1]));
  assign bit_extender_1_out = {{24{multiplexer_1_out[7]}}, multiplexer_1_out};  // Bit_Extender bit_extender_1
  assign bit_extender_2_out = {{24{1'b0}}, multiplexer_1_out};  // Bit_Extender bit_extender_2
  assign bit_extender_3_out = {{16{multiplexer_2_out[15]}}, multiplexer_2_out};  // Bit_Extender bit_extender_3
  assign bit_extender_4_out = {{16{1'b0}}, multiplexer_2_out};  // Bit_Extender bit_extender_4
  Multiplexer #(.select(3), .width(32)) multiplexer_3 (
    .in0(bit_extender_1_out), .in1(bit_extender_3_out), .in2(ram128kb_1_outp), .in3(bit_extender_2_out),
    .in4(bit_extender_4_out), .out(memOut), .sel(funct_3));  // open: in5, in6, in7

  // Notes on the sheet:
  //   byte
  //   halfWord
  //   word
  //   lb
  //   lbu
  //   lh
  //   lhu
  //   lw
endmodule
