// Logisim project RegisterFileModule.circ as structural Verilog: 1 circuit, main circuit RegisterFile32
module RegisterFile32 (
  input  load,
  input  [4:0] rsi1,
  input  [4:0] rsi2,
  input  [4:0] rdi,
  input  [31:0] rd,
  input  Clock,
  output [31:0] rs1,
  output [31:0] rs2
);

  wire demultiplexer_1_out1, demultiplexer_1_out2, demultiplexer_1_out3, demultiplexer_1_out4,
       demultiplexer_1_out5, demultiplexer_1_out6, demultiplexer_1_out7, demultiplexer_1_out8,
       demultiplexer_1_out9, demultiplexer_1_out10, demultiplexer_1_out11, demultiplexer_1_out12,
       demultiplexer_1_out13, demultiplexer_1_out14, demultiplexer_1_out15, demultiplexer_1_out16,
       demultiplexer_1_out17, demultiplexer_1_out18, demultiplexer_1_out19, demultiplexer_1_out20,
       demultiplexer_1_out21, demultiplexer_1_out22, demultiplexer_1_out23, demultiplexer_1_out24,
       demultiplexer_1_out25, demultiplexer_1_out26, demultiplexer_1_out27, demultiplexer_1_out28,
       demultiplexer_1_out29, demultiplexer_1_out30, demultiplexer_1_out31;
  wire [31:0] x1_q, x2_q, x3_q, x4_q, x5_q, x6_q, x7_q, x8_q, x9_q, x10_q, x11_q, x12_q, x13_q, x14_q, x15_q,
       x16_q, x17_q, x18_q, x19_q, x20_q, x21_q, x22_q, x23_q, x24_q, x25_q, x26_q, x27_q, x28_q, x29_q,
       x30_q, x31_q;

  Demultiplexer #(.select(5)) demultiplexer_1 (
    .out1(demultiplexer_1_out1), .out2(demultiplexer_1_out2), .out3(demultiplexer_1_out3),
    .out4(demultiplexer_1_out4), .out5(demultiplexer_1_out5), .out6(demultiplexer_1_out6),
    .out7(demultiplexer_1_out7), .out8(demultiplexer_1_out8), .out9(demultiplexer_1_out9),
    .out10(demultiplexer_1_out10), .out11(demultiplexer_1_out11), .out12(demultiplexer_1_out12),
    .out13(demultiplexer_1_out13), .out14(demultiplexer_1_out14), .out15(demultiplexer_1_out15),
    .out16(demultiplexer_1_out16), .out17(demultiplexer_1_out17), .out18(demultiplexer_1_out18),
    .out19(demultiplexer_1_out19), .out20(demultiplexer_1_out20), .out21(demultiplexer_1_out21),
    .out22(demultiplexer_1_out22), .out23(demultiplexer_1_out23), .out24(demultiplexer_1_out24),
    .out25(demultiplexer_1_out25), .out26(demultiplexer_1_out26), .out27(demultiplexer_1_out27),
    .out28(demultiplexer_1_out28), .out29(demultiplexer_1_out29), .out30(demultiplexer_1_out30),
    .out31(demultiplexer_1_out31), .in(load), .sel(rdi));  // open: out0
  Register #(.width(32)) x4 (.D(rd), .en(demultiplexer_1_out4), .clk(Clock), .Q(x4_q));  // open: clr
  Register #(.width(32)) x8 (.D(rd), .en(demultiplexer_1_out8), .clk(Clock), .Q(x8_q));  // open: clr
  Register #(.width(32)) x12 (.D(rd), .en(demultiplexer_1_out12), .clk(Clock), .Q(x12_q));  // open: clr
  Register #(.width(32)) x16 (.D(rd), .en(demultiplexer_1_out16), .clk(Clock), .Q(x16_q));  // open: clr
  Register #(.width(32)) x20 (.D(rd), .en(demultiplexer_1_out20), .clk(Clock), .Q(x20_q));  // open: clr
  Register #(.width(32)) x24 (.D(rd), .en(demultiplexer_1_out24), .clk(Clock), .Q(x24_q));  // open: clr
  Register #(.width(32)) x28 (.D(rd), .en(demultiplexer_1_out28), .clk(Clock), .Q(x28_q));  // open: clr
  Register #(.width(32)) x1 (.D(rd), .en(demultiplexer_1_out1), .clk(Clock), .Q(x1_q));  // open: clr
  Register #(.width(32)) x5 (.D(rd), .en(demultiplexer_1_out5), .clk(Clock), .Q(x5_q));  // open: clr
  Register #(.width(32)) x9 (.D(rd), .en(demultiplexer_1_out9), .clk(Clock), .Q(x9_q));  // open: clr
  Register #(.width(32)) x13 (.D(rd), .en(demultiplexer_1_out13), .clk(Clock), .Q(x13_q));  // open: clr
  Register #(.width(32)) x17 (.D(rd), .en(demultiplexer_1_out17), .clk(Clock), .Q(x17_q));  // open: clr
  Register #(.width(32)) x21 (.D(rd), .en(demultiplexer_1_out21), .clk(Clock), .Q(x21_q));  // open: clr
  Register #(.width(32)) x25 (.D(rd), .en(demultiplexer_1_out25), .clk(Clock), .Q(x25_q));  // open: clr
  Register #(.width(32)) x29 (.D(rd), .en(demultiplexer_1_out29), .clk(Clock), .Q(x29_q));  // open: clr
  Register #(.width(32)) x2 (.D(rd), .en(demultiplexer_1_out2), .clk(Clock), .Q(x2_q));  // open: clr
  Register #(.width(32)) x6 (.D(rd), .en(demultiplexer_1_out6), .clk(Clock), .Q(x6_q));  // open: clr
  Register #(.width(32)) x10 (.D(rd), .en(demultiplexer_1_out10), .clk(Clock), .Q(x10_q));  // open: clr
  Register #(.width(32)) x14 (.D(rd), .en(demultiplexer_1_out14), .clk(Clock), .Q(x14_q));  // open: clr
  Register #(.width(32)) x18 (.D(rd), .en(demultiplexer_1_out18), .clk(Clock), .Q(x18_q));  // open: clr
  Register #(.width(32)) x22 (.D(rd), .en(demultiplexer_1_out22), .clk(Clock), .Q(x22_q));  // open: clr
  Register #(.width(32)) x26 (.D(rd), .en(demultiplexer_1_out26), .clk(Clock), .Q(x26_q));  // open: clr
  Register #(.width(32)) x30 (.D(rd), .en(demultiplexer_1_out30), .clk(Clock), .Q(x30_q));  // open: clr
  Register #(.width(32)) x3 (.D(rd), .en(demultiplexer_1_out3), .clk(Clock), .Q(x3_q));  // open: clr
  Register #(.width(32)) x7 (.D(rd), .en(demultiplexer_1_out7), .clk(Clock), .Q(x7_q));  // open: clr
  Register #(.width(32)) x11 (.D(rd), .en(demultiplexer_1_out11), .clk(Clock), .Q(x11_q));  // open: clr
  Register #(.width(32)) x15 (.D(rd), .en(demultiplexer_1_out15), .clk(Clock), .Q(x15_q));  // open: clr
  Register #(.width(32)) x19 (.D(rd), .en(demultiplexer_1_out19), .clk(Clock), .Q(x19_q));  // open: clr
  Register #(.width(32)) x23 (.D(rd), .en(demultiplexer_1_out23), .clk(Clock), .Q(x23_q));  // open: clr
  Register #(.width(32)) x27 (.D(rd), .en(demultiplexer_1_out27), .clk(Clock), .Q(x27_q));  // open: clr
  Register #(.width(32)) x31 (.D(rd), .en(demultiplexer_1_out31), .clk(Clock), .Q(x31_q));  // open: clr
  Multiplexer #(.select(5), .width(32)) multiplexer_1 (
    .in0({32{1'b0}}), .in1(x1_q), .in2(x2_q), .in3(x3_q), .in4(x4_q), .in5(x5_q), .in6(x6_q), .in7(x7_q),
    .in8(x8_q), .in9(x9_q), .in10(x10_q), .in11(x11_q), .in12(x12_q), .in13(x13_q), .in14(x14_q),
    .in15(x15_q), .in16(x16_q), .in17(x17_q), .in18(x18_q), .in19(x19_q), .in20(x20_q), .in21(x21_q),
    .in22(x22_q), .in23(x23_q), .in24(x24_q), .in25(x25_q), .in26(x26_q), .in27(x27_q), .in28(x28_q),
    .in29(x29_q), .in30(x30_q), .in31(x31_q), .out(rs1), .sel(rsi1));
  Multiplexer #(.select(5), .width(32)) multiplexer_2 (
    .in0({32{1'b0}}), .in1(x1_q), .in2(x2_q), .in3(x3_q), .in4(x4_q), .in5(x5_q), .in6(x6_q), .in7(x7_q),
    .in8(x8_q), .in9(x9_q), .in10(x10_q), .in11(x11_q), .in12(x15_q), .in13(x14_q), .in14(x13_q),
    .in15(x12_q), .in16(x16_q), .in17(x17_q), .in18(x18_q), .in19(x19_q), .in20(x20_q), .in21(x21_q),
    .in22(x22_q), .in23(x23_q), .in24(x24_q), .in25(x25_q), .in26(x26_q), .in27(x27_q), .in28(x28_q),
    .in29(x29_q), .in30(x30_q), .in31(x31_q), .out(rs2), .sel(rsi2));

  // Notes on the sheet:
  //   x0
endmodule
