// Logisim project components.circ as structural Verilog
module HalfAdder (
  input  a,
  input  b,
  output sum,
  output carry
);

  xor xor_1 (sum, a, b);
  and and_1 (carry, a, b);
endmodule

module FullAdder (
  input  a,
  input  b,
  input  carryIN,
  output carryOUT,
  output sum
);

  wire halfadder_1_carry, halfadder_1_sum, halfadder_2_carry;

  HalfAdder halfadder_1 (.a(a), .b(b), .sum(halfadder_1_sum), .carry(halfadder_1_carry));
  HalfAdder halfadder_2 (.a(halfadder_1_sum), .b(carryIN), .sum(sum), .carry(halfadder_2_carry));
  or or_1 (carryOUT, halfadder_1_carry, halfadder_2_carry);
endmodule

module Adder32 (
  input  [31:0] a,
  input  [31:0] b,
  output [31:0] c
);

  wire fulladder_1_carryout, fulladder_2_carryout, fulladder_3_carryout, fulladder_4_carryout,
       fulladder_5_carryout, fulladder_6_carryout, fulladder_7_carryout, fulladder_8_carryout,
       fulladder_9_carryout, fulladder_10_carryout, fulladder_11_carryout, fulladder_12_carryout,
       fulladder_13_carryout, fulladder_14_carryout, fulladder_15_carryout, fulladder_16_carryout,
       fulladder_17_carryout, fulladder_18_carryout, fulladder_19_carryout, fulladder_20_carryout,
       fulladder_21_carryout, fulladder_22_carryout, fulladder_23_carryout, fulladder_24_carryout,
       fulladder_25_carryout, fulladder_26_carryout, fulladder_27_carryout, fulladder_28_carryout,
       fulladder_29_carryout, fulladder_30_carryout, fulladder_31_carryout;

  FullAdder fulladder_1 (.a(a[0]), .b(b[0]), .carryIN(1'b0), .carryOUT(fulladder_1_carryout), .sum(c[0]));
  FullAdder fulladder_2 (
    .a(a[1]), .b(b[1]), .carryIN(fulladder_1_carryout), .carryOUT(fulladder_2_carryout), .sum(c[1]));
  FullAdder fulladder_3 (
    .a(a[2]), .b(b[2]), .carryIN(fulladder_2_carryout), .carryOUT(fulladder_3_carryout), .sum(c[2]));
  FullAdder fulladder_4 (
    .a(a[3]), .b(b[3]), .carryIN(fulladder_3_carryout), .carryOUT(fulladder_4_carryout), .sum(c[3]));
  FullAdder fulladder_5 (
    .a(a[4]), .b(b[4]), .carryIN(fulladder_4_carryout), .carryOUT(fulladder_5_carryout), .sum(c[4]));
  FullAdder fulladder_6 (
    .a(a[5]), .b(b[5]), .carryIN(fulladder_5_carryout), .carryOUT(fulladder_6_carryout), .sum(c[5]));
  FullAdder fulladder_7 (
    .a(a[6]), .b(b[6]), .carryIN(fulladder_6_carryout), .carryOUT(fulladder_7_carryout), .sum(c[6]));
  FullAdder fulladder_8 (
    .a(a[7]), .b(b[7]), .carryIN(fulladder_7_carryout), .carryOUT(fulladder_8_carryout), .sum(c[7]));
  FullAdder fulladder_9 (
    .a(a[8]), .b(b[8]), .carryIN(fulladder_8_carryout), .carryOUT(fulladder_9_carryout), .sum(c[8]));
  FullAdder fulladder_10 (
    .a(a[9]), .b(b[9]), .carryIN(fulladder_9_carryout), .carryOUT(fulladder_10_carryout), .sum(c[9]));
  FullAdder fulladder_11 (
    .a(a[10]), .b(b[10]), .carryIN(fulladder_10_carryout), .carryOUT(fulladder_11_carryout), .sum(c[10]));
  FullAdder fulladder_12 (
    .a(a[11]), .b(b[11]), .carryIN(fulladder_11_carryout), .carryOUT(fulladder_12_carryout), .sum(c[11]));
  FullAdder fulladder_13 (
    .a(a[12]), .b(b[12]), .carryIN(fulladder_12_carryout), .carryOUT(fulladder_13_carryout), .sum(c[12]));
  FullAdder fulladder_14 (
    .a(a[13]), .b(b[13]), .carryIN(fulladder_13_carryout), .carryOUT(fulladder_14_carryout), .sum(c[13]));
  FullAdder fulladder_15 (
    .a(a[14]), .b(b[14]), .carryIN(fulladder_14_carryout), .carryOUT(fulladder_15_carryout), .sum(c[14]));
  FullAdder fulladder_16 (
    .a(a[15]), .b(b[15]), .carryIN(fulladder_15_carryout), .carryOUT(fulladder_16_carryout), .sum(c[15]));
  FullAdder fulladder_17 (
    .a(a[16]), .b(b[16]), .carryIN(fulladder_16_carryout), .carryOUT(fulladder_17_carryout), .sum(c[16]));
  FullAdder fulladder_18 (
    .a(a[17]), .b(b[17]), .carryIN(fulladder_17_carryout), .carryOUT(fulladder_18_carryout), .sum(c[17]));
  FullAdder fulladder_19 (
    .a(a[18]), .b(b[18]), .carryIN(fulladder_18_carryout), .carryOUT(fulladder_19_carryout), .sum(c[18]));
  FullAdder fulladder_20 (
    .a(a[19]), .b(b[19]), .carryIN(fulladder_19_carryout), .carryOUT(fulladder_20_carryout), .sum(c[19]));
  FullAdder fulladder_21 (
    .a(a[20]), .b(b[20]), .carryIN(fulladder_20_carryout), .carryOUT(fulladder_21_carryout), .sum(c[20]));
  FullAdder fulladder_22 (
    .a(a[21]), .b(b[21]), .carryIN(fulladder_21_carryout), .carryOUT(fulladder_22_carryout), .sum(c[21]));
  FullAdder fulladder_23 (
    .a(a[22]), .b(b[22]), .carryIN(fulladder_22_carryout), .carryOUT(fulladder_23_carryout), .sum(c[22]));
  FullAdder fulladder_24 (
    .a(a[23]), .b(b[23]), .carryIN(fulladder_23_carryout), .carryOUT(fulladder_24_carryout), .sum(c[23]));
  FullAdder fulladder_25 (
    .a(a[24]), .b(b[24]), .carryIN(fulladder_24_carryout), .carryOUT(fulladder_25_carryout), .sum(c[24]));
  FullAdder fulladder_26 (
    .a(a[25]), .b(b[25]), .carryIN(fulladder_25_carryout), .carryOUT(fulladder_26_carryout), .sum(c[25]));
  FullAdder fulladder_27 (
    .a(a[26]), .b(b[26]), .carryIN(fulladder_26_carryout), .carryOUT(fulladder_27_carryout), .sum(c[26]));
  FullAdder fulladder_28 (
    .a(a[27]), .b(b[27]), .carryIN(fulladder_27_carryout), .carryOUT(fulladder_28_carryout), .sum(c[27]));
  FullAdder fulladder_29 (
    .a(a[28]), .b(b[28]), .carryIN(fulladder_28_carryout), .carryOUT(fulladder_29_carryout), .sum(c[28]));
  FullAdder fulladder_30 (
    .a(a[29]), .b(b[29]), .carryIN(fulladder_29_carryout), .carryOUT(fulladder_30_carryout), .sum(c[29]));
  FullAdder fulladder_31 (
    .a(a[30]), .b(b[30]), .carryIN(fulladder_30_carryout), .carryOUT(fulladder_31_carryout), .sum(c[30]));
  FullAdder fulladder_32 (.a(a[31]), .b(b[31]), .carryIN(fulladder_31_carryout), .sum(c[31]));  // open: carryOUT
endmodule

module Increment32 (
  input  [31:0] in_1,
  output [31:0] out_2
);

  Adder32 adder32_1 (.a(in_1), .b(32'h1), .c(out_2));
endmodule
